# Fritzing sketch sketch (saved by Fritzing 0.9.2b)
circuit board: 14.2262cm x 8.7cm

parts:
  Out1_(0x20) = IC, DIP package, 28 pins [chip_label=MCP23017]
  Out2_(0x21) = IC, DIP package, 28 pins [chip_label=MCP23017]
  In2_(0x23) = IC, DIP package, 28 pins [chip_label=MCP23017]
  U5 = IC, DIP package, 16 pins [chip_label=LTV847]
  R17 = Resistor [tolerance=±10% resistance=470 package=THT]
  R18 = Resistor [tolerance=±10% resistance=470 package=THT]
  R19 = Resistor [tolerance=±10% resistance=470 package=THT]
  R20 = Resistor [tolerance=±10% resistance=470 package=THT]
  U6 = IC, DIP package, 16 pins [chip_label=LTV847]
  R21 = Resistor [tolerance=±10% resistance=470 package=THT]
  R23 = Resistor [tolerance=±10% resistance=470 package=THT]
  R24 = Resistor [tolerance=±10% resistance=470 package=THT]
  R22 = Resistor [tolerance=±10% resistance=470 package=THT]
  U7 = IC, DIP package, 16 pins [chip_label=LTV847]
  R27 = Resistor [tolerance=±10% resistance=470 package=THT]
  R28 = Resistor [tolerance=±10% resistance=470 package=THT]
  R26 = Resistor [tolerance=±10% resistance=470 package=THT]
  R25 = Resistor [tolerance=±10% resistance=470 package=THT]
  U8 = IC, DIP package, 16 pins [chip_label=LTV847]
  R29 = Resistor [tolerance=±10% resistance=470 package=THT]
  R30 = Resistor [tolerance=±10% resistance=470 package=THT]
  R31 = Resistor [tolerance=±10% resistance=470 package=THT]
  R32 = Resistor [tolerance=±10% resistance=470 package=THT]
  In1_(0x22) = IC, DIP package, 28 pins [chip_label=MCP23017]
  U3 = IC, DIP package, 16 pins [chip_label=LTV847]
  U1 = IC, DIP package, 16 pins [chip_label=LTV847]
  U4 = IC, DIP package, 16 pins [chip_label=LTV847]
  U2 = IC, DIP package, 16 pins [chip_label=LTV847]
  R10 = Resistor [tolerance=±10% resistance=470 package=THT]
  R9 = Resistor [tolerance=±10% resistance=470 package=THT]
  R12 = Resistor [tolerance=±10% resistance=470 package=THT]
  R5 = Resistor [tolerance=±10% resistance=470 package=THT]
  R7 = Resistor [tolerance=±10% resistance=470 package=THT]
  R11 = Resistor [tolerance=±10% resistance=470 package=THT]
  R1 = Resistor [tolerance=±10% resistance=470 package=THT]
  R6 = Resistor [tolerance=±10% resistance=470 package=THT]
  R14 = Resistor [tolerance=±10% resistance=470 package=THT]
  R8 = Resistor [tolerance=±10% resistance=470 package=THT]
  R3 = Resistor [tolerance=±10% resistance=470 package=THT]
  R2 = Resistor [tolerance=±10% resistance=470 package=THT]
  R13 = Resistor [tolerance=±10% resistance=470 package=THT]
  R4 = Resistor [tolerance=±10% resistance=470 package=THT]
  R16 = Resistor [tolerance=±10% resistance=470 package=THT]
  R15 = Resistor [tolerance=±10% resistance=470 package=THT]
  J1 = shrouded pin header, 40 pins [form="♂ (shrouded male)"]
  3_3V_DC = Power plug
  13V_DC = Power plug
  J4 = male pin header, 8 pins [form="♂ (male)"]
  J5 = male pin header, 8 pins [form="♂ (male)"]
  J3 = male pin header, 8 pins [form="♂ (male)"]
  J2 = male pin header, 8 pins [form="♂ (male)"]

nets:
  3.3V IN/RESET: Out1_(0x20).pin9, Out1_(0x20).pin18, Out2_(0x21).pin9, Out2_(0x21).pin15, Out2_(0x21).pin18, In2_(0x23).pin9, In2_(0x23).pin15, In2_(0x23).pin16, In2_(0x23).pin18, U5.pin10, U5.pin12, U5.pin14, U5.pin16, U6.pin10, U6.pin12, U6.pin14, U6.pin16, U7.pin10, U7.pin12, U7.pin14, U7.pin16, U8.pin10, U8.pin12, U8.pin14, U8.pin16, In1_(0x22).pin9, In1_(0x22).pin16, In1_(0x22).pin18, U3.pin10, U3.pin12, U3.pin14, U3.pin16, U1.pin10, U1.pin12, U1.pin14, U1.pin16, U4.pin10, U4.pin12, U4.pin14, U4.pin16, U2.pin10, U2.pin12, U2.pin14, U2.pin16, 3_3V_DC.VCC
  3.3V GND: Out1_(0x20).pin10, Out1_(0x20).pin15, Out1_(0x20).pin16, Out1_(0x20).pin17, Out2_(0x21).pin10, Out2_(0x21).pin16, Out2_(0x21).pin17, In2_(0x23).pin10, In2_(0x23).pin17, In1_(0x22).pin10, In1_(0x22).pin15, In1_(0x22).pin17, 3_3V_DC.GND
  SCL: Out1_(0x20).pin12, Out2_(0x21).pin12, In2_(0x23).pin12, In1_(0x22).pin12, J1.pin3
  SDA: Out1_(0x20).pin13, Out2_(0x21).pin13, In2_(0x23).pin13, In1_(0x22).pin13, J1.pin2
  N1: In2_(0x23).pin1, U7.pin15
  N2: In2_(0x23).pin2, U7.pin13
  N3: In2_(0x23).pin3, U7.pin11
  N4: In2_(0x23).pin4, U7.pin9
  N5: In2_(0x23).pin5, U8.pin15
  N6: In2_(0x23).pin6, U8.pin13
  N7: In2_(0x23).pin7, U8.pin11
  N8: In2_(0x23).pin8, U8.pin9
  N9: In2_(0x23).pin21, U5.pin15
  N10: In2_(0x23).pin22, U5.pin13
  N11: In2_(0x23).pin23, U5.pin11
  N12: In2_(0x23).pin24, U5.pin9
  N13: In2_(0x23).pin25, U6.pin15
  N14: In2_(0x23).pin26, U6.pin13
  N15: In2_(0x23).pin27, U6.pin11
  N16: In2_(0x23).pin28, U6.pin9
  N17: U5.pin1, R17.Pin_0
  13V GND: U5.pin2, U5.pin4, U5.pin6, U5.pin8, U6.pin2, U6.pin4, U6.pin6, U6.pin8, U7.pin2, U7.pin4, U7.pin6, U7.pin8, U8.pin2, U8.pin4, U8.pin6, U8.pin8, U3.pin2, U3.pin4, U3.pin6, U3.pin8, U1.pin2, U1.pin4, U1.pin6, U1.pin8, U4.pin2, U4.pin4, U4.pin6, U4.pin8, U2.pin2, U2.pin4, U2.pin6, U2.pin8, 13V_DC.GND
  N18: U5.pin3, R18.Pin_0
  N19: U5.pin5, R19.Pin_0
  N20: U5.pin7, R20.Pin_0
  N21: R17.Pin_1, J4.pin1
  N22: R18.Pin_1, J4.pin2
  N23: R19.Pin_1, J4.pin3
  N24: R20.Pin_1, J4.pin4
  N25: U6.pin1, R21.Pin_0
  N26: U6.pin3, R22.Pin_0
  N27: U6.pin5, R23.Pin_0
  N28: U6.pin7, R24.Pin_0
  N29: R21.Pin_1, J4.pin5
  N30: R23.Pin_1, J4.pin7
  N31: R24.Pin_1, J4.pin8
  N32: R22.Pin_1, J4.pin6
  N33: U7.pin1, R25.Pin_1
  N34: U7.pin3, R26.Pin_1
  N35: U7.pin5, R27.Pin_1
  N36: U7.pin7, R28.Pin_1
  N37: R27.Pin_0, J5.pin3
  N38: R28.Pin_0, J5.pin4
  N39: R26.Pin_0, J5.pin2
  N40: R25.Pin_0, J5.pin1
  N41: U8.pin1, R29.Pin_1
  N42: U8.pin3, R30.Pin_1
  N43: U8.pin5, R31.Pin_1
  N44: U8.pin7, R32.Pin_1
  N45: R29.Pin_0, J5.pin5
  N46: R30.Pin_0, J5.pin6
  N47: R31.Pin_0, J5.pin7
  N48: R32.Pin_0, J5.pin8
  N49: In1_(0x22).pin1, U3.pin15
  N50: In1_(0x22).pin2, U3.pin13
  N51: In1_(0x22).pin3, U3.pin11
  N52: In1_(0x22).pin4, U3.pin9
  N53: In1_(0x22).pin5, U4.pin15
  N54: In1_(0x22).pin6, U4.pin13
  N55: In1_(0x22).pin7, U4.pin11
  N56: In1_(0x22).pin8, U4.pin9
  N57: In1_(0x22).pin21, U1.pin15
  N58: In1_(0x22).pin22, U1.pin13
  N59: In1_(0x22).pin23, U1.pin11
  N60: In1_(0x22).pin24, U1.pin9
  N61: In1_(0x22).pin25, U2.pin15
  N62: In1_(0x22).pin26, U2.pin13
  N63: In1_(0x22).pin27, U2.pin11
  N64: In1_(0x22).pin28, U2.pin9
  N65: U3.pin1, R9.Pin_1
  N66: U3.pin3, R10.Pin_1
  N67: U3.pin5, R11.Pin_1
  N68: U3.pin7, R12.Pin_1
  N69: U1.pin1, R1.Pin_0
  N70: U1.pin3, R2.Pin_0
  N71: U1.pin5, R3.Pin_0
  N72: U1.pin7, R4.Pin_0
  N73: U4.pin1, R13.Pin_1
  N74: U4.pin3, R14.Pin_1
  N75: U4.pin5, R15.Pin_1
  N76: U4.pin7, R16.Pin_1
  N77: U2.pin1, R5.Pin_0
  N78: U2.pin3, R6.Pin_0
  N79: U2.pin5, R7.Pin_0
  N80: U2.pin7, R8.Pin_0
  N81: R10.Pin_0, J3.pin2
  N82: R9.Pin_0, J3.pin1
  N83: R12.Pin_0, J3.pin4
  N84: R5.Pin_1, J2.pin5
  N85: R7.Pin_1, J2.pin7
  N86: R11.Pin_0, J3.pin3
  N87: R1.Pin_1, J2.pin1
  N88: R6.Pin_1, J2.pin6
  N89: R14.Pin_0, J3.pin6
  N90: R8.Pin_1, J2.pin8
  N91: R3.Pin_1, J2.pin3
  N92: R2.Pin_1, J2.pin2
  N93: R13.Pin_0, J3.pin5
  N94: R4.Pin_1, J2.pin4
  N95: R16.Pin_0, J3.pin8
  N96: R15.Pin_0, J3.pin7
  13V IN: 13V_DC.VCC

notes:
  0
